# Fritzing sketch schematic (saved by Fritzing 0.9.10b)
perfboards: 1

parts:
  U7 = atmega328 [package=dip]
  S5_(Reset) = Momentary Switch [package=ksa_sealed_tac_switch]
  Y4 = CRYSTAL [package=crystal-smd-5x3]
  LED2_(Power) = LED - 3mm [color="Red (633nm)" current=0.030 package="3 mm [THT]"]
  R152_(Power) = Resistor [tolerance=±5% power=0.25 resistance=680 package=THT]
  C12_(Cyrstal_2) = Ceramic Capacitor [capacitance=22pF voltage=35V package="100 mil [THT, multilayer]"]
  C14_(DTR/Reset) = Ceramic Capacitor [capacitance=100nF voltage=35V package="100 mil [THT, multilayer]"]
  C15_(Power_decouple) = Electrolytic Capacitor [capacitance=10µF voltage=35V package="100 mil [THT, electrolytic]"]
  Part1 = FTDI Basic Programmer
  C19_(IC_Decouple) = Ceramic Capacitor [capacitance=100nF voltage=35V package="200 mil [THT, multilayer]"]
  R222_(Activity) = Resistor [tolerance=±5% power=0.25 resistance=680 package=THT]
  LED1_(Activity) = LED - 3mm [color="Green (560nm)" current=0.030 package="3 mm [THT]"]
  C12_(Cyrstal_1) = Ceramic Capacitor [capacitance=22pF voltage=35V package="100 mil [THT, multilayer]"]
  R221_(Reset_pull_up) = Resistor [tolerance=±5% power=0.25 resistance=10k package=THT]
  J2 = male pin header, 14 pins [form="♂ (male)"]
  J3 = male pin header, 14 pins [form="♂ (male)"]

nets (from the schematic view):
  N1: U7.RESET, J3.pin14
  N2: U7.D0_(RX), Part1.TXO, J3.pin13
  N3: U7.D1_(TX), Part1.RXI, J3.pin12
  N4: U7.D2, J3.pin11
  N5: U7.D3_(PWM), J3.pin10
  N6: U7.D4, J3.pin9
  5V: U7.VCC, R152_(Power).Pin_0, C15_(Power_decouple).+, Part1.POWER, C19_(IC_Decouple).1, R221_(Reset_pull_up).Pin_0, J3.pin8
  GND: U7.GND, S5_(Reset).1, LED2_(Power).cathode, C12_(Cyrstal_2).0, C15_(Power_decouple).-, Part1.GND, C19_(IC_Decouple).0, R222_(Activity).Pin_1, C12_(Cyrstal_1).0, J2.pin7, J3.pin7
  N7: U7.XLAT1, Y4.1, C12_(Cyrstal_1).1, J3.pin6
  N8: U7.XLAT2, Y4.2, C12_(Cyrstal_2).1, J3.pin5
  N9: U7.D5_(PWM), J3.pin4
  N10: U7.D6_(PWM), J3.pin3
  N11: U7.D7, J3.pin2
  N12: U7.D8, J3.pin1
  N13: U7.D9_(PWM), J2.pin14
  N14: U7.D10_(PWM), J2.pin13
  N15: U7.D11_(PWM), J2.pin12
  N16: U7.D12, J2.pin11
  N17: U7.D13, LED1_(Activity).anode, J2.pin10
  N18: U7.AVCC, J2.pin9
  N19: U7.AREF, J2.pin8
  N20: U7.A0, J2.pin6
  N21: U7.A1, J2.pin5
  N22: U7.A2, J2.pin4
  N23: U7.A3, J2.pin3
  N24: U7.A4, J2.pin2
  N25: U7.A5, J2.pin1
  N26: S5_(Reset).3, C14_(DTR/Reset).0, R221_(Reset_pull_up).Pin_1
  N27: LED2_(Power).anode, R152_(Power).Pin_1
  N28: C14_(DTR/Reset).1, Part1.DTR
  N29: R222_(Activity).Pin_0, LED1_(Activity).cathode
